# Fritzing sketch water_level_wiring_diagram (saved by Fritzing 0.9.5d)
breadboards: 1

parts:
  Water_Level_Sensor1 = Water Level Sensor
  Mod1 = Raspberry Pi 4B
  KEYPAD1 = Membrane Matrix Keypad
  IC1 = IC, DIP package, 28 pins [chip_label=ATmega88PA]
  R1 = Resistor [tolerance=±5% resistance=10k package=THT]
  L1 = Inductor [package="400 mil [THT]"]
  C1 = Ceramic Capacitor [capacitance=100nF package="100 mil [THT, multilayer]"]
  C2 = Ceramic Capacitor [capacitance=100nF package="100 mil [THT, multilayer]"]
  C3 = Electrolytic Capacitor [capacitance=1µF package="100 mil [THT, electrolytic]"]
  R4 = Resistor [tolerance=±5% resistance=100 package=THT]
  R5 = Resistor [tolerance=±5% resistance=100 package=THT]
  R6 = Resistor [tolerance=±5% resistance=100 package=THT]
  LED1 = LED - 5mm [color="Red (633nm)" package="5 mm [THT]"]
  LED2 = LED - 5mm [color="Yellow (585nm)" package="5 mm [THT]"]
  LED3 = LED - 5mm [color="Green (555nm)" package="5 mm [THT]"]

nets:
  N1: Water_Level_Sensor1.SIG, IC1.pin23
  VCC: Water_Level_Sensor1.VCC, Mod1.3V3, IC1.pin7, R1.Pin_1, L1.pin_0, C1.0, C3.+
  GND: Water_Level_Sensor1.GND, Mod1.GND, IC1.pin8, IC1.pin22, C1.1, C2.0, C3.-, R4.Pin_1, R5.Pin_1, R6.Pin_1
  N2: Mod1.GPIO14, IC1.pin2
  N3: Mod1.GPIO15, IC1.pin3
  N4: Mod1.GPIO17, LED1.anode
  N5: Mod1.GPIO27, LED2.anode
  N6: Mod1.GPIO22, LED3.anode
  N7: Mod1.GPIO12, KEYPAD1.1
  N8: Mod1.GPIO13, KEYPAD1.7
  N9: Mod1.GPIO19, KEYPAD1.6
  N10: Mod1.GPIO16, KEYPAD1.2
  N11: Mod1.GPIO26, KEYPAD1.5
  N12: Mod1.GPIO20, KEYPAD1.3
  N13: Mod1.GPIO21, KEYPAD1.4
  N14: IC1.pin1, R1.Pin_0
  N15: IC1.pin20, L1.pin_1, C2.1
  N16: R4.Pin_0, LED3.cathode
  N17: R5.Pin_0, LED2.cathode
  N18: R6.Pin_0, LED1.cathode

custom parts:
  Water Level Sensor: A water level sensor. This sensor operates at 3V to 5V. The Sig (signal) pin outputs an analogue signal that is in proportion to the amount of water in contact with the sensor.
  Membrane Matrix Keypad: Membrane Matrix 3x4 Keypad
